// Logisim project contadorGray.circ as structural Verilog: 1 circuit, main circuit main
module main (
  input  Clock,
  output [3:0] out_2
);

  wire and_1_out, and_2_out, and_3_out, and_4_out, and_5_out, and_6_out, and_7_out, and_8_out, and_9_out,
       and_10_out, and_11_out, and_12_out, and_13_out, and_14_out, and_15_out, and_16_out, or_1_out,
       or_2_out, or_3_out, or_4_out, Q0_qn, Q1_qn, Q2_qn, Q3_qn;

  and and_1 (and_1_out, Q3_qn, Q2_qn, Q1_qn, Q0_qn);
  and and_2 (and_2_out, Q3_qn, out_2[2], out_2[1], Q0_qn);
  and and_3 (and_3_out, out_2[3], Q2_qn, out_2[1], Q0_qn);
  and and_4 (and_4_out, out_2[3], out_2[2], Q1_qn, Q0_qn);
  and and_5 (and_5_out, Q3_qn, Q2_qn, out_2[1], out_2[0]);
  and and_6 (and_6_out, Q3_qn, out_2[2], Q1_qn, out_2[0]);
  and and_7 (and_7_out, out_2[3], Q2_qn, Q1_qn, out_2[0]);
  and and_8 (and_8_out, out_2[3], out_2[2], out_2[1], out_2[0]);
  or or_1 (or_1_out, and_1_out, and_2_out, and_3_out, and_4_out);
  or or_2 (or_2_out, and_5_out, and_6_out, and_7_out, and_8_out);
  J_K_Flip_Flop Q0 (.J(or_1_out), .K(or_2_out), .clk(Clock), .Q(out_2[0]), .Qn(Q0_qn));  // open: preset, reset
  and and_9 (and_9_out, Q3_qn, Q2_qn, out_2[0]);
  and and_10 (and_10_out, out_2[3], out_2[2], out_2[0]);
  and and_11 (and_11_out, Q3_qn, out_2[2], out_2[0]);
  and and_12 (and_12_out, out_2[3], Q2_qn, out_2[0]);
  or or_3 (or_3_out, and_9_out, and_10_out);
  J_K_Flip_Flop Q1 (.J(or_3_out), .K(or_4_out), .clk(Clock), .Q(out_2[1]), .Qn(Q1_qn));  // open: preset, reset
  or or_4 (or_4_out, and_11_out, and_12_out);
  and and_13 (and_13_out, Q3_qn, out_2[1], Q0_qn);
  J_K_Flip_Flop Q2 (.J(and_13_out), .K(and_14_out), .clk(Clock), .Q(out_2[2]), .Qn(Q2_qn));  // open: preset, reset
  and and_14 (and_14_out, out_2[3], out_2[1], Q0_qn);
  and and_15 (and_15_out, out_2[2], Q1_qn, Q0_qn);
  and and_16 (and_16_out, Q2_qn, Q1_qn, Q0_qn);
  J_K_Flip_Flop Q3 (.J(and_15_out), .K(and_16_out), .clk(Clock), .Q(out_2[3]), .Qn(Q3_qn));  // open: preset, reset

  // Notes on the sheet:
  //   Luan Alecxander Krzyzaniak
endmodule
